// Logisim project test1.circ as structural Verilog: 2 circuits, main circuit main
module main (
  input  in_1,
  input  in_2,
  input  in_3,
  input  in_4,
  input  in_5
);

  comparador_1_bit comparador_1_bit_1 (
    .E_int(in_1), .G_int(in_2), .L_int(in_3), .P(in_4), .T(in_5));  // open: E_out, G_out, L_out
  comparador_1_bit comparador_1_bit_2 ();  // open: E_int, G_int, L_int, P, T, E_out, G_out, L_out
  comparador_1_bit comparador_1_bit_3 ();  // open: E_int, G_int, L_int, P, T, E_out, G_out, L_out
endmodule

module comparador_1_bit (
  input  E_int,
  input  G_int,
  input  L_int,
  input  P,
  input  T,
  output E_out,
  output G_out,
  output L_out
);

  wire and_1_out, and_2_out, and_3_out, and_4_out, not_1_out, not_2_out, not_3_out, xor_1_out;

  not not_1 (not_1_out, P);
  not not_2 (not_2_out, T);
  xor xor_1 (xor_1_out, P, T);
  and and_1 (and_1_out, not_1_out, T);
  and and_2 (and_2_out, P, not_2_out);
  not not_3 (not_3_out, xor_1_out);
  and and_3 (and_3_out, E_int, and_1_out);
  and and_4 (and_4_out, E_int, and_2_out);
  and and_5 (E_out, E_int, not_3_out);
  or or_1 (L_out, L_int, and_3_out);
  or or_2 (G_out, G_int, and_4_out);
endmodule
